# Fritzing sketch Diseño de proyecto Huella (saved by Fritzing 0.9.3b)
breadboards: 2

parts:
  YwRobot_Power_Supply1 = YwRobot Breadboard Power Supply [part_number=545043]
  SG1 = Buzzer 12mm [package=buzzer-ccv-kit]
  U1 = ESP32-30Pin [part_number=ESP32-30Pin]
  LED1 = RGB LED (com. cathode, rgb) [package="5 mm [THT]"]
  R4 = Resistor [tolerance=±5% resistance=220 package=THT]
  Componente1 = sensor_biometrico

nets:
  N1: YwRobot_Power_Supply1.VCC#5, R4.Pin_1, Componente1.VCC
  N2: YwRobot_Power_Supply1.GND#13, LED1.blue_anode, Componente1.GND
  N3: SG1.1, R4.Pin_0
  N4: U1.D13, LED1.red_anode
  N5: U1.D12, LED1.common_cathode
  N6: U1.D14, LED1.green_anode
  N7: U1.RX0, Componente1.TX
  N8: U1.TX0, Componente1.RX

custom parts:
  YwRobot Breadboard Power Supply: The YwRobot Breadboard Power Supply (MB-V2) has two power rails; they can be 5V or 3V3. Power to the module can be provided through the female USB socket or through the A10 (female) 2.1mm power jack.
  ESP32-30Pin: Generic 30-Pin ESP32
  sensor_biometrico: Adafruit Optical Fingerprint Sensor
