# Fritzing sketch Diseño de proyecto Huella (saved by Fritzing 0.9.3b)
breadboards: 1

parts:
  YwRobot_Power_Supply1 = YwRobot Breadboard Power Supply [part_number=545043]
  LED1 = LED - 5mm [color="Red (633nm)" package="5 mm [THT]"]
  LED2 = LED - 5mm [color="Blue (430nm)" package="5 mm [THT]"]
  SG1 = Buzzer 12mm [package=buzzer-ccv-kit]
  U1 = ESP32-30Pin [part_number=ESP32-30Pin]
  R1 = Resistor [tolerance=±5% resistance=220 package=THT]
  R2 = Resistor [tolerance=±5% resistance=220 package=THT]
  R3 = Resistor [tolerance=±5% resistance=220 package=THT]
  LED3 = LED - 5mm [color="Green (555nm)" package="5 mm [THT]"]
  R4 = Resistor [tolerance=±5% resistance=220 package=THT]
  Componente1 = sensor_biometrico  # not connected

nets:
  N1: YwRobot_Power_Supply1.VCC#5, YwRobot_Power_Supply1.VCC#6
  N2: YwRobot_Power_Supply1.VCC#9, YwRobot_Power_Supply1.VCC#10, U1.D26
  N3: YwRobot_Power_Supply1.GND#11, YwRobot_Power_Supply1.GND#12, U1.D23, R1.Pin_1, R2.Pin_1, R3.Pin_1, R4.Pin_1
  N4: YwRobot_Power_Supply1.GND#13, YwRobot_Power_Supply1.GND#14
  N5: LED1.cathode, R1.Pin_0
  N6: LED2.cathode, R2.Pin_0
  N7: SG1.1, R4.Pin_0
  N8: SG1.2, U1.VIN
  N9: R3.Pin_0, LED3.cathode

custom parts:
  YwRobot Breadboard Power Supply: The YwRobot Breadboard Power Supply (MB-V2) has two power rails; they can be 5V or 3V3. Power to the module can be provided through the female USB socket or through the A10 (female) 2.1mm power jack.
  ESP32-30Pin: Generic 30-Pin ESP32
  sensor_biometrico: Adafruit Optical Fingerprint Sensor
