# Fritzing sketch Untitled Sketch (saved by Fritzing 0.9.3b)
breadboards: 2

parts:
  YwRobot_Power_Supply1 = YwRobot Breadboard Power Supply [part_number=545043]
  U1 = ESP32-30Pin [part_number=ESP32-30Pin]
  DHT11_1 = DHT11 module

nets:
  N1: YwRobot_Power_Supply1.VCC#5, YwRobot_Power_Supply1.VCC#6
  N2: YwRobot_Power_Supply1.VCC#9, YwRobot_Power_Supply1.VCC#10
  N3: YwRobot_Power_Supply1.GND#11, YwRobot_Power_Supply1.GND#12
  N4: YwRobot_Power_Supply1.GND#13, YwRobot_Power_Supply1.GND#14
  3V3: U1.3v3, DHT11_1.VCC
  N5: U1.GND#16, DHT11_1.GND
  N6: U1.D15, DHT11_1.DATA

custom parts:
  YwRobot Breadboard Power Supply: The YwRobot Breadboard Power Supply (MB-V2) has two power rails; they can be 5V or 3V3. Power to the module can be provided through the female USB socket or through the A10 (female) 2.1mm power jack.
  ESP32-30Pin: Generic 30-Pin ESP32
  DHT11 module: DHT11 black pcb module
